# Fritzing sketch Esquema (saved by Fritzing 0.9.5d)

parts:
  Módulo_Comparador = FC-28 Soil Hygrometer Module
  NodeMCU = NodeMCU V1.0
  Módulo_Relé_5v = KY-019 5V Relay Module [package="Breakout board"]
  Válvula_Solenoide_12v = Solenoid
  Fonte_12v = Power plug
  Sonda_de_Umidade = FC-28 Soil Hygrometer Module - Probe
  Módulo_Regulador_Lm7805 = AMS1117 step down module

nets:
  VCC: Módulo_Comparador.VCC, NodeMCU.3V3
  N1: Módulo_Comparador.GND, NodeMCU.GND#13, Módulo_Relé_5v.-
  N2: Módulo_Comparador.AO, NodeMCU.A0
  N3: Módulo_Comparador.POS, Sonda_de_Umidade.POS
  N4: Módulo_Comparador.NEG, Sonda_de_Umidade.NEG
  N5: NodeMCU.D1, Módulo_Relé_5v.S
  N6: NodeMCU.Vin, Módulo_Relé_5v.+, Módulo_Regulador_Lm7805.VOUT+
  N7: NodeMCU.GND#16, Válvula_Solenoide_12v.pin1, Fonte_12v.GND, Módulo_Regulador_Lm7805.GND-
  N8: Módulo_Relé_5v.NC, Válvula_Solenoide_12v.pin2
  N9: Módulo_Relé_5v.Common, Fonte_12v.VCC, Módulo_Regulador_Lm7805.VIN+

notes:
  Legenda:
  - Preto: GND
  - Lilás: +12v
  - Vermelho: +5v
  - Laranja: +3.3v
  - Amarelo: ANALOG
  - Verde: SIGNAL

custom parts:
  FC-28 Soil Hygrometer Module: The FC-28 is a soil hygrometer module that uses the Texas Instruments LM393 comparator chip to provide an analog measurement of soil humidity. The digital output is high when soil moisture is over a certain threshold, as determined by adjusting the potentiometer.
  NodeMCU V1.0: ESP8266 based NodeMCU V1.0
  KY-019 5V Relay Module: KY-019 5V Relay module, used to control AC circuits. (Special thanks to vanepp for fixing the PCB holes and other errors)
  FC-28 Soil Hygrometer Module - Probe: The FC-28 is a soil hygrometer module that uses the Texas Instruments LM393 comparator chip to provide an analog measurement of soil humidity.
