# Fritzing sketch Diagramas (saved by Fritzing 0.9.5d)

parts:
  NodeMCU = NodeMCU V1.0
  Módulo_Relé_5v = KY-019 5V Relay Module [package="Breakout board"]
  Válvula_Solenoide_12v = Solenoid
  Fonte_12v = Power plug
  Sonda_de_Umidade = FC-28 Soil Hygrometer Module - Probe
  Step-Down_12v_-_5v = RioRand LM2596
  Módulo_Comparador = FC-28 Soil Hygrometer Module

nets:
  N1: NodeMCU.D1, Módulo_Relé_5v.S
  N2: NodeMCU.3V3#5, Módulo_Relé_5v.+
  N3: NodeMCU.GND#6, Módulo_Relé_5v.-
  N4: NodeMCU.Vin, Step-Down_12v_-_5v.Pin_3
  N5: NodeMCU.GND#16, Step-Down_12v_-_5v.Pin_4
  N6: NodeMCU.3V3#19, Módulo_Comparador.VCC
  N7: NodeMCU.GND#33, Módulo_Comparador.GND
  N8: NodeMCU.A0, Módulo_Comparador.AO
  N9: Módulo_Relé_5v.NC, Válvula_Solenoide_12v.pin2
  N10: Módulo_Relé_5v.Common, Fonte_12v.VCC, Step-Down_12v_-_5v.Pin_1
  N11: Válvula_Solenoide_12v.pin1, Fonte_12v.GND, Step-Down_12v_-_5v.Pin_2
  N12: Sonda_de_Umidade.POS, Módulo_Comparador.POS
  N13: Sonda_de_Umidade.NEG, Módulo_Comparador.NEG

notes:
  Legenda:
  - Preto GND
  - Vermelho +12v
  - Laranja +5v
  - Amarelo +3.3v
  - Verde SIGNAL
  - Azul ANALOG

custom parts:
  NodeMCU V1.0: ESP8266 based NodeMCU V1.0
  KY-019 5V Relay Module: KY-019 5V Relay module, used to control AC circuits. (Special thanks to vanepp for fixing the PCB holes and other errors)
  FC-28 Soil Hygrometer Module - Probe: The FC-28 is a soil hygrometer module that uses the Texas Instruments LM393 comparator chip to provide an analog measurement of soil humidity.
  FC-28 Soil Hygrometer Module: The FC-28 is a soil hygrometer module that uses the Texas Instruments LM393 comparator chip to provide an analog measurement of soil humidity. The digital output is high when soil moisture is over a certain threshold, as determined by adjusting the potentiometer.
